# Fritzing sketch Dog Ball Launcher Fritzing  (saved by Fritzing 0.9.4)
breadboards: 1

parts:
  OLED_I2C1 = OLED 128x64 I2C Monochrome Display
  Teensy_3_1 = Teensy 3.1
  S1 = Pushbutton [package="[THT]"]
  WIZ820io1 = WIZ820io [part_number=WIZ820io]
  Relay1 = Relay - 6 pins [package="DIP (Dual Inline) [THT]"]
  J1 = Power Jack [package=power_jack_pth]
  M1 = DC Motor
  Part1 = 12 NeoPixel Ring [part_number=1643]
  R1 = Resistor [tolerance=±5% resistance=220 package="2512 [SMD]"]
  R2 = Resistor [tolerance=±5% resistance=220 package="2512 [SMD]"]
  LED1 = LEDs [package=led10mm]
  P1 = S1133 Si Photodiode [package="8mm Ceramic [THT]"]
  J2 = Basic Servo
  M2 = DC Motor

nets:
  N1: OLED_I2C1.SDA, Teensy_3_1.A4/D18
  N2: OLED_I2C1.SCK, Teensy_3_1.A5/D19
  VDD: OLED_I2C1.VDD, Teensy_3_1.Vin, S1.Pin_1, S1.Pin_2, WIZ820io1.VIN, Relay1.VCC, Part1.VDD, LED1.C, P1.anode, J2.vcc
  GND: OLED_I2C1.GND, Teensy_3_1.GND, WIZ820io1.GND, Relay1.GND, Part1.GND, R1.Pin_1, R2.Pin_1, LED1.A, J2.gnd
  N3: Teensy_3_1.D7, Part1.IN
  N4: Teensy_3_1.D8, S1.Pin_3, S1.Pin_4, R2.Pin_0
  N5: Teensy_3_1.D9, WIZ820io1.nRESET
  N6: Teensy_3_1.D10, WIZ820io1.nSS
  N7: Teensy_3_1.D11, WIZ820io1.MOSI
  N8: Teensy_3_1.D12, WIZ820io1.MISO
  N9: Teensy_3_1.D13, WIZ820io1.SCLK
  N10: Teensy_3_1.A3/D17, Relay1.IN
  N11: Teensy_3_1.A6/D20, J2.pulse
  N12: Teensy_3_1.A9/D23, R1.Pin_0, P1.cathode
  N13: Relay1.COM, J1.GND
  N14: Relay1.ON, M1.pin_2, M2.pin_1
  N15: J1.GNDBREAK, M1.pin_1, M2.pin_2

custom parts:
  Pushbutton: A generic pushbutton.
  Relay - 6 pins: A DIP stand-in part for whatever IC you want. With 6 pins on a 900mil dual inline package (DIP) footprint.
  12 NeoPixel Ring: 12 ultra bright smart LED NeoPixels are arranged in a circle with 1.5" (37mm) outer diameter. The rings are 'chainable' - connect the output pin of one to the input pin of another. Use only one microcontroller pin to control as many as you can chain together! Each LED is addressable as the driver chip is inside the LED. Each one has ~18mA constant current drive so the color will be very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
